// Logisim project 32bCPU.circ as structural Verilog: 30 circuits, main circuit Datapath
module Datapath (
  input  [1:0] in_1,
  output [31:0] out_2
);

  wire asel_t, brancher_1_breq, brancher_1_brlt, bsel_t, clk_t, contollogic_1_bne, contollogic_1_regwena,
       fwe_t, isFPU_t, PCsel_t, pred_t, taken_t, we_t;
  wire [2:0] contollogic_1_immsel;
  wire [3:0] contollogic_1_alusel;
  wire [7:0] bitselector_1_out, shifter_1_out;
  wire [31:0] adder_1_out, ALU_A, B_t, branchpred_1_tadd, D_t, dataA_t, dataB_t, DMEM_WB_out2, EX_DMEM_out1,
       floatregfile_1_rs1, floatregfile_1_rs2, FPU_1_out_4, ID_EX_out1, ID_EX_out3, immgen_1_imm31_0, ins_t,
       lw_t, multiplexer_1_out, multiplexer_4_out, PC2_t, PC2P4_t, PC_t, PCP4_t, PCp4_t_t, ram_1_dout,
       regctl_1_rs1, regctl_1_rs2, regfile_1_rs1, regfile_1_rs2, register_1_q, register_3_q, rom_1_data;

  Multiplexer #(.width(32)) multiplexer_1 (.in0(PCp4_t_t), .in1(ALU_A), .out(multiplexer_1_out), .sel(PCsel_t));
  // Probe on multiplexer_1_out
  PC pc_1 (.inPC(multiplexer_1_out), .clk(clk_t), .outPCp4(PCp4_t_t), .outPC(PC_t));
  Clock clock_1 (.out(clk_t));
  BranchPred branchpred_1 (.PC(PC_t), .Taken(taken_t), .ALU_a(ALU_A), .clk(clk_t), .Tadd(branchpred_1_tadd));
  ROM #(.addrWidth(10), .dataWidth(32)) rom_1 (.addr(branchpred_1_tadd[11:2]), .data(rom_1_data));
  SCPred scpred_1 (.out_3(pred_t));  // open: D, in_2
  IFPipe IF_ID (.In1(rom_1_data), .clk(clk_t), .Out1(ins_t));  // open: Stall, Flush
  Register #(.width(32)) register_1 (.D(PC_t), .clk(clk_t), .Q(register_1_q));  // open: en, clr
  RegFile regfile_1 (
    .we(we_t), .rsi1(ins_t[19:15]), .rsi2(ins_t[24:20]), .rdi(ins_t[11:7]), .rd(ALU_A), .clk(clk_t),
    .rs1(regfile_1_rs1), .rs2(regfile_1_rs2));
  FloatRegFile floatregfile_1 (
    .we(fwe_t), .rsi1(ins_t[19:15]), .rsi2(ins_t[24:20]), .rdi(ins_t[11:7]), .clk(clk_t),
    .rs1(floatregfile_1_rs1), .rs2(floatregfile_1_rs2));  // open: rd
  // Probe on ins_t
  PipelineReg ID_EX (
    .In1(regctl_1_rs1), .In2(regctl_1_rs2), .In3(immgen_1_imm31_0), .clk(clk_t), .Out1(ID_EX_out1),
    .Out2(B_t), .Out3(ID_EX_out3));  // open: Stall, Flush
  RegCtl regctl_1 (
    .rsi1(regfile_1_rs1), .rsi1_2(floatregfile_1_rs1), .rsi2(regfile_1_rs2), .rsi2_2(floatregfile_1_rs2),
    .isFPU(isFPU_t), .rs1(regctl_1_rs1), .rs2(regctl_1_rs2));
  immGen immgen_1 (.ins(ins_t), .sel(contollogic_1_immsel), .imm31_0(immgen_1_imm31_0));
  Register #(.width(32)) register_2 (.D(register_1_q), .clk(clk_t), .Q(PC2_t));  // open: en, clr
  Multiplexer #(.width(32)) multiplexer_2 (.in0(ID_EX_out1), .in1(PC2_t), .out(dataA_t), .sel(asel_t));
  Brancher brancher_1 (
    .dataA(ID_EX_out1), .dataB(B_t), .brUn(contollogic_1_bne), .brLt(brancher_1_brlt), .brEq(brancher_1_breq));
  Multiplexer #(.width(32)) multiplexer_3 (.in0(B_t), .in1(ID_EX_out3), .out(dataB_t), .sel(bsel_t));
  ContolLogic contollogic_1 (
    .ins(ins_t), .BrEq(brancher_1_breq), .BrLt(brancher_1_brlt), .ALUsel(contollogic_1_alusel),
    .regwena(contollogic_1_regwena), .immsel(contollogic_1_immsel), .asel(asel_t), .bsel(bsel_t),
    .isFPU(isFPU_t), .PCsel(PCsel_t), .Taken(taken_t), .BNE(contollogic_1_bne));
  ALU ALU_1 (.dataA(dataA_t), .dataB(dataB_t), .sel(contollogic_1_alusel), .dataD(ALU_A));
  // Probe on ALU_A
  FPU FPU_1 (.in_1(dataA_t), .in_2(dataB_t), .in_3(contollogic_1_alusel), .out_4(FPU_1_out_4));
  Multiplexer #(.width(32)) multiplexer_4 (.in0(ALU_A), .in1(FPU_1_out_4), .out(multiplexer_4_out), .sel(isFPU_t));
  Demultiplexer demultiplexer_1 (.out0(we_t), .out1(fwe_t), .in(contollogic_1_regwena), .sel(isFPU_t));
  EXPipe EX_DMEM (.In1(multiplexer_4_out), .clk(clk_t), .Out1(EX_DMEM_out1));  // open: Stall, Flush
  Register #(.width(32)) register_3 (.D(PC2_t), .clk(clk_t), .Q(register_3_q));  // open: en, clr
  BitSelector #(.group(8), .width(32)) bitselector_1 (.in(EX_DMEM_out1), .out(bitselector_1_out), .sel(2'b00));
  RAM #(.dataWidth(32)) ram_1 (.addr(shifter_1_out), .clk(clk_t), .din(B_t), .dout(ram_1_dout));  // open: we, oe
  Shifter #(.shift("lr")) shifter_1 (.in(bitselector_1_out), .\dist (3'b010), .out(shifter_1_out));
  Adder #(.width(32)) adder_1 (.a(register_3_q), .b(32'h4), .out(adder_1_out));  // open: cin, cout
  LoadCtl loadctl_1 (.A(ALU_A), .lw_t(lw_t), .D(D_t));  // open: Isel, wbsel
  DMEMpipe DMEM_WB (
    .In1(adder_1_out), .In2(EX_DMEM_out1), .In3(ram_1_dout), .clk(clk_t), .Out1(PC2P4_t),
    .Out2(DMEM_WB_out2), .Out3(lw_t));  // open: Stall, Flush
  Multiplexer #(.select(2), .width(32)) multiplexer_5 (
    .in0(lw_t), .in1(DMEM_WB_out2), .in2(PCP4_t), .out(out_2), .sel(in_1));  // open: in3

  // Other names for the same wires on the sheet: rdi_t[4:0] = ins_t[11:7]; rsi1_t[4:0] = ins_t[19:15];
  //   rsi2_t[4:0] = ins_t[24:20]

  // Notes on the sheet:
  //   contents of rom_1 (hex, n*v repeats v):
  //   8663 fff08093 ff9ff0ef 13
endmodule

// g
module PC (
  input  [31:0] inPC,
  input  clk,
  output [31:0] outPCp4,
  output [31:0] outPC
);

  Register #(.width(32)) register_1 (.D(inPC), .en(1'b1), .clk(clk), .Q(outPC));  // open: clr
  Adder #(.width(32)) adder_1 (.a(outPC), .b(32'h4), .out(outPCp4));  // open: cin, cout

  // Other names for the same wires on the sheet: clk_t = clk; inPC_t[31:0] = inPC; outPC_t[31:0] = outPC;
  //   outPCp4_t[31:0] = outPCp4
endmodule

module RegFile (
  input  [4:0] rsi1,
  input  [4:0] rsi2,
  input  [4:0] rdi,
  input  [31:0] rd,
  input  clk,
  input  we,
  output [31:0] rs1,
  output [31:0] rs2
);

  wire r0we_t, r1we_t, r2we_t, r3we_t, r4we_t, r5we_t, r6we_t, r7we_t, r8we_t, r9we_t, r10we_t, r11we_t,
       r12we_t, r13we_t, r14we_t, r15we_t, r16we_t, r17we_t, r18we_t, r19we_t, r20we_t, r21we_t, r22we_t,
       r23we_t, r24we_t, r25we_t, r26we_t, r27we_t, r28we_t, r29we_t, r30we_t, r31we_t;
  wire [31:0] x1q_t, x2q_t, x3q_t, x4q_t, x5q_t, x6q_t, x7q_t, x8q_t, x9q_t, x10q_t, x11q_t, x12q_t, x13q_t,
       x14q_t, x15q_t, x16q_t, x17q_t, x18q_t, x19q_t, x20q_t, x21q_t, x22q_t, x23q_t, x24q_t, x25q_t,
       x26q_t, x27q_t, x28q_t, x29q_t, x30q_t, x31q_t;

  Demultiplexer #(.select(5)) demultiplexer_1 (
    .out0(r0we_t), .out1(r1we_t), .out2(r2we_t), .out3(r3we_t), .out4(r4we_t), .out5(r5we_t), .out6(r6we_t),
    .out7(r7we_t), .out8(r8we_t), .out9(r9we_t), .out10(r10we_t), .out11(r11we_t), .out12(r12we_t),
    .out13(r13we_t), .out14(r14we_t), .out15(r15we_t), .out16(r16we_t), .out17(r17we_t), .out18(r18we_t),
    .out19(r19we_t), .out20(r20we_t), .out21(r21we_t), .out22(r22we_t), .out23(r23we_t), .out24(r24we_t),
    .out25(r25we_t), .out26(r26we_t), .out27(r27we_t), .out28(r28we_t), .out29(r29we_t), .out30(r30we_t),
    .out31(r31we_t), .in(we), .sel(rdi));
  Register #(.width(32)) x4 (.D(rd), .en(r4we_t), .clk(clk), .Q(x4q_t));  // open: clr
  Register #(.width(32)) x8 (.D(rd), .en(r8we_t), .clk(clk), .Q(x8q_t));  // open: clr
  Register #(.width(32)) x12 (.D(rd), .en(r12we_t), .clk(clk), .Q(x12q_t));  // open: clr
  Register #(.width(32)) x16 (.D(rd), .en(r16we_t), .clk(clk), .Q(x16q_t));  // open: clr
  Register #(.width(32)) x20 (.D(rd), .en(r20we_t), .clk(clk), .Q(x20q_t));  // open: clr
  Register #(.width(32)) x24 (.D(rd), .en(r24we_t), .clk(clk), .Q(x24q_t));  // open: clr
  Register #(.width(32)) x28 (.D(rd), .en(r28we_t), .clk(clk), .Q(x28q_t));  // open: clr
  Register #(.width(32)) x1 (.D(rd), .en(r1we_t), .clk(clk), .Q(x1q_t));  // open: clr
  Register #(.width(32)) x5 (.D(rd), .en(r5we_t), .clk(clk), .Q(x5q_t));  // open: clr
  Register #(.width(32)) x9 (.D(rd), .en(r9we_t), .clk(clk), .Q(x9q_t));  // open: clr
  Register #(.width(32)) x13 (.D(rd), .en(r13we_t), .clk(clk), .Q(x13q_t));  // open: clr
  Register #(.width(32)) x17 (.D(rd), .en(r17we_t), .clk(clk), .Q(x17q_t));  // open: clr
  Register #(.width(32)) x21 (.D(rd), .en(r21we_t), .clk(clk), .Q(x21q_t));  // open: clr
  Register #(.width(32)) x25 (.D(rd), .en(r25we_t), .clk(clk), .Q(x25q_t));  // open: clr
  Register #(.width(32)) x29 (.D(rd), .en(r29we_t), .clk(clk), .Q(x29q_t));  // open: clr
  Register #(.width(32)) x2 (.D(rd), .en(r2we_t), .clk(clk), .Q(x2q_t));  // open: clr
  Register #(.width(32)) x6 (.D(rd), .en(r6we_t), .clk(clk), .Q(x6q_t));  // open: clr
  Register #(.width(32)) x10 (.D(rd), .en(r10we_t), .clk(clk), .Q(x10q_t));  // open: clr
  Register #(.width(32)) x14 (.D(rd), .en(r14we_t), .clk(clk), .Q(x14q_t));  // open: clr
  Register #(.width(32)) x18 (.D(rd), .en(r18we_t), .clk(clk), .Q(x18q_t));  // open: clr
  Register #(.width(32)) x22 (.D(rd), .en(r22we_t), .clk(clk), .Q(x22q_t));  // open: clr
  Register #(.width(32)) x26 (.D(rd), .en(r26we_t), .clk(clk), .Q(x26q_t));  // open: clr
  Register #(.width(32)) x30 (.D(rd), .en(r30we_t), .clk(clk), .Q(x30q_t));  // open: clr
  Register #(.width(32)) x3 (.D(rd), .en(r3we_t), .clk(clk), .Q(x3q_t));  // open: clr
  Register #(.width(32)) x7 (.D(rd), .en(r7we_t), .clk(clk), .Q(x7q_t));  // open: clr
  Register #(.width(32)) x11 (.D(rd), .en(r11we_t), .clk(clk), .Q(x11q_t));  // open: clr
  Register #(.width(32)) x15 (.D(rd), .en(r15we_t), .clk(clk), .Q(x15q_t));  // open: clr
  Register #(.width(32)) x19 (.D(rd), .en(r19we_t), .clk(clk), .Q(x19q_t));  // open: clr
  Register #(.width(32)) x23 (.D(rd), .en(r23we_t), .clk(clk), .Q(x23q_t));  // open: clr
  Register #(.width(32)) x27 (.D(rd), .en(r27we_t), .clk(clk), .Q(x27q_t));  // open: clr
  Register #(.width(32)) x31 (.D(rd), .en(r31we_t), .clk(clk), .Q(x31q_t));  // open: clr
  Multiplexer #(.select(5), .width(32)) multiplexer_1 (
    .in0({32{1'b0}}), .in1(x1q_t), .in2(x2q_t), .in3(x3q_t), .in4(x4q_t), .in5(x5q_t), .in6(x6q_t),
    .in7(x7q_t), .in8(x8q_t), .in9(x9q_t), .in10(x10q_t), .in11(x11q_t), .in12(x12q_t), .in13(x13q_t),
    .in14(x14q_t), .in15(x15q_t), .in16(x16q_t), .in17(x17q_t), .in18(x18q_t), .in19(x19q_t), .in20(x20q_t),
    .in21(x21q_t), .in22(x22q_t), .in23(x23q_t), .in24(x24q_t), .in25(x25q_t), .in26(x26q_t), .in27(x27q_t),
    .in28(x28q_t), .in29(x29q_t), .in30(x30q_t), .in31(x31q_t), .out(rs1), .sel(rsi1));
  Multiplexer #(.select(5), .width(32)) multiplexer_2 (
    .in0({32{1'b0}}), .in1(x1q_t), .in2(x2q_t), .in3(x3q_t), .in4(x4q_t), .in5(x5q_t), .in6(x6q_t),
    .in7(x7q_t), .in8(x8q_t), .in9(x9q_t), .in10(x10q_t), .in11(x11q_t), .in12(x12q_t), .in13(x13q_t),
    .in14(x14q_t), .in15(x15q_t), .in16(x16q_t), .in17(x17q_t), .in18(x18q_t), .in19(x19q_t), .in20(x20q_t),
    .in21(x21q_t), .in22(x22q_t), .in23(x23q_t), .in24(x24q_t), .in25(x25q_t), .in26(x26q_t), .in27(x27q_t),
    .in28(x28q_t), .in29(x29q_t), .in30(x30q_t), .in31(x31q_t), .out(rs2), .sel(rsi2));

  // Other names for the same wires on the sheet: clk_t = clk; rd_t[31:0] = rd; rdi_t[4:0] = rdi; rs1_t[31:0] = rs1;
  //   rs2_t[31:0] = rs2; rsi1_t[4:0] = rsi1; rsi2_t[4:0] = rsi2
endmodule

module ALU (
  input  [31:0] dataA,
  input  [31:0] dataB,
  input  [3:0] sel,
  output [31:0] dataD
);

  wire comparator_1_lt, comparator_2_lt;
  wire [31:0] addOut_t, andOut_t, orOut_t, sllOut_t, sltOut_t, sltuOut_t, sraOut_t, srlOut_t, subOut_t,
       xorOut_t;

  Adder #(.width(32)) adder_1 (.a(dataA), .b(dataB), .out(addOut_t));  // open: cin, cout
  Subtractor #(.width(32)) subtractor_1 (.a(dataA), .b(dataB), .out(subOut_t));  // open: bin, bout
  Shifter #(.width(32)) shifter_1 (.in(dataA), .\dist (dataB[4:0]), .out(sllOut_t));
  Comparator #(.width(32)) comparator_1 (.a(dataA), .b(dataB), .lt(comparator_1_lt));  // open: gt, eq
  Comparator #(.mode("unsigned"), .width(32)) comparator_2 (
    .a(dataA), .b(dataB), .lt(comparator_2_lt));  // open: gt, eq
  assign xorOut_t = dataA ^ dataB;  // XOR_Gate xor_1, 32 bits wide
  Shifter #(.shift("lr"), .width(32)) shifter_2 (.in(dataA), .\dist (dataB[4:0]), .out(srlOut_t));
  Shifter #(.shift("ar"), .width(32)) shifter_3 (.in(dataA), .\dist (dataB[4:0]), .out(sraOut_t));
  assign orOut_t = dataA | dataB;  // OR_Gate or_1, 32 bits wide
  assign andOut_t = dataA & dataB;  // AND_Gate and_1, 32 bits wide
  Multiplier #(.width(32)) multiplier_1 ();  // open: a, b, out, cin, cout
  assign sltOut_t = {{31{1'b0}}, comparator_1_lt};  // Bit_Extender bit_extender_1
  assign sltuOut_t = {{31{1'b0}}, comparator_2_lt};  // Bit_Extender bit_extender_2
  Multiplexer #(.select(4), .width(32)) multiplexer_1 (
    .in0(addOut_t), .in1(sllOut_t), .in2(sltOut_t), .in3(sltuOut_t), .in4(xorOut_t), .in5(srlOut_t),
    .in6(orOut_t), .in7(andOut_t), .in8(subOut_t), .in13(sraOut_t), .out(dataD), .sel(sel));  // open: in9, in10, in11, in12, in14, in15

  // Other names for the same wires on the sheet: dataA_t[31:0] = dataA; dataB_t[31:0] = dataB;
  //   dataBL5_t[4:0] = dataB[4:0]; dataD_t[31:0] = dataD; sel_t[3:0] = sel
endmodule

module immGen (
  input  [31:0] ins,
  input  [2:0] sel,
  output [31:0] imm31_0
);

  wire [3:0] bsplitter_1_imm4_1;
  wire [4:0] ssplitter_1_imm4_0;
  wire [5:0] bsplitter_1_imm10_5;
  wire [6:0] ssplitter_1_imm11_5;
  wire [7:0] jsplitter_1_imm19_12;
  wire [9:0] jsplitter_1_imm10_1;
  wire [11:0] isplitter_1_imm11_0;
  wire [12:11] bsplitter_1_imm11;
  wire [20:11] jsplitter_1_imm11;
  wire [31:0] BOut_t, IOut_t, JOut_t, SOut_t;
  wire [31:12] UOut_t;

  Clock clock_1 ();  // open: out
  ISplitter isplitter_1 (.ins(ins), .imm11_0(isplitter_1_imm11_0));  // open: opcode, rd, rs1, funct3
  SSplitter ssplitter_1 (
    .ins(ins), .imm11_5(ssplitter_1_imm11_5), .imm4_0(ssplitter_1_imm4_0));  // open: opcode, rs1, rs2, funct3
  BSplitter bsplitter_1 (
    .ins(ins), .imm12(bsplitter_1_imm11[12]), .imm11(bsplitter_1_imm11[11]), .imm4_1(bsplitter_1_imm4_1),
    .imm10_5(bsplitter_1_imm10_5));  // open: opcode, funct3, rs1, rs2
  JSplitter jsplitter_1 (
    .ins(ins), .imm10_1(jsplitter_1_imm10_1), .imm19_12(jsplitter_1_imm19_12), .imm11(jsplitter_1_imm11[11]),
    .imm20(jsplitter_1_imm11[20]));  // open: opcode, rd
  USplitter usplitter_1 (.ins(ins), .imm31_12(UOut_t));  // open: rd, opcode
  assign IOut_t = {{20{isplitter_1_imm11_0[11]}}, isplitter_1_imm11_0};  // Bit_Extender bit_extender_1
  assign SOut_t = {{20{ssplitter_1_imm11_5[6]}}, {ssplitter_1_imm11_5, ssplitter_1_imm4_0}};  // Bit_Extender bit_extender_2
  assign BOut_t = {{19{bsplitter_1_imm11[12]}}, {bsplitter_1_imm11, bsplitter_1_imm10_5, bsplitter_1_imm4_1, 1'b0}};  // Bit_Extender bit_extender_3
  assign JOut_t = {{11{jsplitter_1_imm11[20]}}, {jsplitter_1_imm11[20], jsplitter_1_imm19_12, jsplitter_1_imm11[11], jsplitter_1_imm10_1, 1'b0}};  // Bit_Extender bit_extender_4
  Multiplexer #(.select(3), .width(32)) multiplexer_1 (
    .in0(IOut_t), .in1(SOut_t), .in2(BOut_t), .in3(JOut_t), .in4({UOut_t, {12{1'b0}}}), .out(imm31_0),
    .sel(sel));  // open: in5, in6, in7

  // Other names for the same wires on the sheet: imm31_0_t[31:0] = imm31_0; ins_t[31:0] = ins; sel_t[2:0] = sel
endmodule

module ISplitter (
  input  [31:0] ins,
  output [6:0] opcode,
  output [4:0] rd,
  output [2:0] funct3,
  output [4:0] rs1,
  output [11:0] imm11_0
);


  assign funct3 = ins[14:12];
  assign imm11_0 = ins[31:20];
  assign opcode = ins[6:0];
  assign rd = ins[11:7];
  assign rs1 = ins[19:15];
endmodule

module SSplitter (
  input  [31:0] ins,
  output [6:0] opcode,
  output [4:0] imm4_0,
  output [2:0] funct3,
  output [4:0] rs1,
  output [4:0] rs2,
  output [6:0] imm11_5
);


  assign funct3 = ins[14:12];
  assign imm4_0 = ins[11:7];
  assign imm11_5 = ins[31:25];
  assign opcode = ins[6:0];
  assign rs1 = ins[19:15];
  assign rs2 = ins[24:20];
endmodule

module USplitter (
  input  [31:0] ins,
  output [6:0] opcode,
  output [4:0] rd,
  output [19:0] imm31_12
);


  assign imm31_12 = ins[31:12];
  assign opcode = ins[6:0];
  assign rd = ins[11:7];
endmodule

module JSplitter (
  input  [31:0] ins,
  output [6:0] opcode,
  output [4:0] rd,
  output [7:0] imm19_12,
  output imm11,
  output [9:0] imm10_1,
  output imm20
);


  assign imm10_1 = ins[30:21];
  assign imm11 = ins[20];
  assign imm19_12 = ins[19:12];
  assign imm20 = ins[31];
  assign opcode = ins[6:0];
  assign rd = ins[11:7];
endmodule

module BSplitter (
  input  [31:0] ins,
  output [6:0] opcode,
  output imm11,
  output [3:0] imm4_1,
  output [2:0] funct3,
  output [4:0] rs1,
  output [4:0] rs2,
  output imm12,
  output [5:0] imm10_5
);


  assign funct3 = ins[14:12];
  assign imm4_1 = ins[11:8];
  assign imm10_5 = ins[30:25];
  assign imm11 = ins[7];
  assign imm12 = ins[31];
  assign opcode = ins[6:0];
  assign rs1 = ins[19:15];
  assign rs2 = ins[24:20];
endmodule

module Brancher (
  input  [31:0] dataA,
  input  [31:0] dataB,
  input  brUn,
  output brLt,
  output brEq
);

  wire comparator_1_lt, comparator_2_lt;

  Comparator #(.width(32)) comparator_1 (.a(dataA), .b(dataB), .eq(brEq), .lt(comparator_1_lt));  // open: gt
  Comparator #(.mode("unsigned"), .width(32)) comparator_2 (
    .a(dataA), .b(dataB), .lt(comparator_2_lt));  // open: gt, eq
  Multiplexer multiplexer_1 (.in0(comparator_1_lt), .in1(comparator_2_lt), .out(brLt), .sel(brUn));

  // Other names for the same wires on the sheet: brEq_t = brEq; brLt_t = brLt; brUn_t = brUn; dataA_t[31:0] = dataA;
  //   dataB_t[31:0] = dataB
endmodule

module ContolLogic (
  input  BrEq,
  input  BrLt,
  input  [31:0] ins,
  output [3:0] ALUsel,
  output regwena,
  output [2:0] immsel,
  output asel,
  output bsel,
  output isFPU,
  output Taken,
  output BNE,
  output PCsel
);

  wire and_1_out, and_2_out, and_3_out, and_4_out, and_5_out, beq_t, bge_t, bgeu_t, blt_t, bltu_t,
       clock_1_out, clock_2_out, clock_4_out, jal_t, not_1_out, or_2_out, PCsel_t;
  wire [10:2] register_1_q;
  wire [18:0] A_t, register_2_q, register_3_q;

  ROM #(.addrWidth(9), .dataWidth(19)) rom_1 (
    .addr({ins[30], ins[14:12], ins[6:2]}), .data({A_t[18:11], isFPU, A_t[9:5], immsel, A_t[1:0]}));
  Register #(.width(19)) register_1 (
    .D({A_t[18:11], isFPU, A_t[9:5], immsel, A_t[1:0]}), .clk(clock_1_out),
    .Q({beq_t, PCsel_t, BNE, blt_t, bge_t, bltu_t, bgeu_t, jal_t, register_1_q[10], ALUsel, regwena, register_1_q[4:2], bsel, asel}));  // open: en, clr
  Clock clock_1 (.out(clock_1_out));
  Register #(.width(19)) register_2 (
    .D({beq_t, PCsel_t, BNE, blt_t, bge_t, bltu_t, bgeu_t, jal_t, register_1_q[10], ALUsel, regwena, register_1_q[4:2], bsel, asel}),
    .clk(clock_2_out), .Q(register_2_q));  // open: en, clr
  Clock clock_2 (.out(clock_2_out));
  Clock clock_3 ();  // open: out
  and and_1 (and_1_out, PCsel_t, jal_t);
  and and_2 (and_2_out, Taken, PCsel_t);
  not not_1 (not_1_out, BrLt);
  or or_1 (PCsel, and_1_out, and_2_out);
  Register #(.width(19)) register_3 (.D(register_2_q), .clk(clock_4_out), .Q(register_3_q));  // open: en, clr
  Clock clock_4 (.out(clock_4_out));
  or or_2 (or_2_out, BrEq, not_1_out);
  and and_3 (and_3_out, beq_t, BrEq);
  and and_4 (and_4_out, blt_t, BrLt);
  and and_5 (and_5_out, or_2_out, bge_t);
  or or_3 (Taken, jal_t, and_3_out, and_4_out, and_5_out);

  // Other names for the same wires on the sheet: i2_t = ins[2]; i3_t = ins[3]; i4_t = ins[4]; i5_t = ins[5];
  //   i6_t = ins[6]; i12_t = ins[12]; i13_t = ins[13]; i14_t = ins[14]; i30_t = ins[30]; asel_t = asel; bsel_t = bsel;
  //   regwena_t = regwena; bne_t = BNE; A_t (some bits) = {isFPU, immsel}; isFPU_t = isFPU; as0_t = ALUsel[0];
  //   as1_t = ALUsel[1]; as2_t = ALUsel[2]; as3_t = ALUsel[3]; is0_t = immsel[0]; is1_t = immsel[1];
  //   is2_t = immsel[2]; taken_t = Taken

  // Notes on the sheet:
  //   contents of rom_1 (hex, n*v repeats v):
  //   4*0 22 7*0 20 7*0 420 0 0 0 6000b 11*0 62 7*0 60 7*0 460 0 0 0 3000b 11*0 a2 7*0 a0 7*0 4a0 15*0 e2
  //   7*0 e0 23*0 122 7*0 120 11*0 2800b 11*0 162 7*0 160 11*0 2400b 11*0 1a2 7*0 1a0 11*0 2200b 11*0 1e2
  //   7*0 1e0 11*0 2100b 11*0 22 7*0 220 7*0 620 143*0 362 7*0 360 78*0 2080f
endmodule

module RSplitter (
  input  [31:0] ins,
  output [6:0] opcode,
  output [4:0] rd,
  output [2:0] funct3,
  output [4:0] rs1,
  output [4:0] rs2,
  output [6:0] funct7
);


  assign funct3 = ins[14:12];
  assign funct7 = ins[31:25];
  assign opcode = ins[6:0];
  assign rd = ins[11:7];
  assign rs1 = ins[19:15];
  assign rs2 = ins[24:20];
endmodule

module ALUCtl (
  input  [31:0] rs2,
  input  [31:0] imm31_0,
  input  Bsel,
  output [31:0] dataB
);
endmodule

module FPU (
  input  [31:0] in_1,
  input  [31:0] in_2,
  input  [3:0] in_3,
  output [31:0] out_4
);

  wire [31:0] addOut_t, divOut_t, multOut_t, subOut_t;

  FPAdder fpadder_1 (.a(in_1), .b(in_2), .out(addOut_t));
  FPSubtractor fpsubtractor_1 (.a(in_1), .b(in_2), .out(subOut_t));
  FPMultiplier fpmultiplier_1 (.a(in_1), .b(in_2), .out(multOut_t));
  FPDivider fpdivider_1 (.a(in_1), .b(in_2), .out(divOut_t));
  // FPComparator fpcomparator_1: pin names not known; wires that end beside it: in_1, in_2
  // FPToInt fptoint_1: pin names not known; wires that end beside it: in_1
  // IntToFP inttofp_1: pin names not known
  Multiplexer #(.select(4), .width(32)) multiplexer_1 (
    .in0(addOut_t), .in1(multOut_t), .in2(divOut_t), .in8(subOut_t), .out(out_4), .sel(in_3));  // open: in3, in4, in5, in6, in7, in9, in10, in11, in12, in13, in14, in15

  // Other names for the same wires on the sheet: dataA_t[31:0] = in_1; dataB_t[31:0] = in_2; sel_t[3:0] = in_3
endmodule

module FloatRegFile (
  input  [4:0] rsi1,
  input  [4:0] rsi2,
  input  [4:0] rdi,
  input  [31:0] rd,
  input  clk,
  input  we,
  output [31:0] rs1,
  output [31:0] rs2
);

  wire r0we_t, r1we_t, r2we_t, r3we_t, r4we_t, r5we_t, r6we_t, r7we_t, r8we_t, r9we_t, r10we_t, r11we_t,
       r12we_t, r13we_t, r14we_t, r15we_t, r16we_t, r17we_t, r18we_t, r19we_t, r20we_t, r21we_t, r22we_t,
       r23we_t, r24we_t, r25we_t, r26we_t, r27we_t, r28we_t, r29we_t, r30we_t, r31we_t;
  wire [31:0] x1q_t, x2q_t, x3q_t, x4q_t, x5q_t, x6q_t, x7q_t, x8q_t, x9q_t, x10q_t, x11q_t, x12q_t, x13q_t,
       x14q_t, x15q_t, x16q_t, x17q_t, x18q_t, x19q_t, x20q_t, x21q_t, x22q_t, x23q_t, x24q_t, x25q_t,
       x26q_t, x27q_t, x28q_t, x29q_t, x30q_t, x31q_t;

  Demultiplexer #(.select(5)) demultiplexer_1 (
    .out0(r0we_t), .out1(r1we_t), .out2(r2we_t), .out3(r3we_t), .out4(r4we_t), .out5(r5we_t), .out6(r6we_t),
    .out7(r7we_t), .out8(r8we_t), .out9(r9we_t), .out10(r10we_t), .out11(r11we_t), .out12(r12we_t),
    .out13(r13we_t), .out14(r14we_t), .out15(r15we_t), .out16(r16we_t), .out17(r17we_t), .out18(r18we_t),
    .out19(r19we_t), .out20(r20we_t), .out21(r21we_t), .out22(r22we_t), .out23(r23we_t), .out24(r24we_t),
    .out25(r25we_t), .out26(r26we_t), .out27(r27we_t), .out28(r28we_t), .out29(r29we_t), .out30(r30we_t),
    .out31(r31we_t), .in(we), .sel(rdi));
  Register #(.width(32)) x4 (.D(rd), .en(r4we_t), .clk(clk), .Q(x4q_t));  // open: clr
  Register #(.width(32)) x8 (.D(rd), .en(r8we_t), .clk(clk), .Q(x8q_t));  // open: clr
  Register #(.width(32)) x12 (.D(rd), .en(r12we_t), .clk(clk), .Q(x12q_t));  // open: clr
  Register #(.width(32)) x16 (.D(rd), .en(r16we_t), .clk(clk), .Q(x16q_t));  // open: clr
  Register #(.width(32)) x20 (.D(rd), .en(r20we_t), .clk(clk), .Q(x20q_t));  // open: clr
  Register #(.width(32)) x24 (.D(rd), .en(r24we_t), .clk(clk), .Q(x24q_t));  // open: clr
  Register #(.width(32)) x28 (.D(rd), .en(r28we_t), .clk(clk), .Q(x28q_t));  // open: clr
  Register #(.width(32)) x1 (.D(rd), .en(r1we_t), .clk(clk), .Q(x1q_t));  // open: clr
  Register #(.width(32)) x5 (.D(rd), .en(r5we_t), .clk(clk), .Q(x5q_t));  // open: clr
  Register #(.width(32)) x9 (.D(rd), .en(r9we_t), .clk(clk), .Q(x9q_t));  // open: clr
  Register #(.width(32)) x13 (.D(rd), .en(r13we_t), .clk(clk), .Q(x13q_t));  // open: clr
  Register #(.width(32)) x17 (.D(rd), .en(r17we_t), .clk(clk), .Q(x17q_t));  // open: clr
  Register #(.width(32)) x21 (.D(rd), .en(r21we_t), .clk(clk), .Q(x21q_t));  // open: clr
  Register #(.width(32)) x25 (.D(rd), .en(r25we_t), .clk(clk), .Q(x25q_t));  // open: clr
  Register #(.width(32)) x29 (.D(rd), .en(r29we_t), .clk(clk), .Q(x29q_t));  // open: clr
  Register #(.width(32)) x2 (.D(rd), .en(r2we_t), .clk(clk), .Q(x2q_t));  // open: clr
  Register #(.width(32)) x6 (.D(rd), .en(r6we_t), .clk(clk), .Q(x6q_t));  // open: clr
  Register #(.width(32)) x10 (.D(rd), .en(r10we_t), .clk(clk), .Q(x10q_t));  // open: clr
  Register #(.width(32)) x14 (.D(rd), .en(r14we_t), .clk(clk), .Q(x14q_t));  // open: clr
  Register #(.width(32)) x18 (.D(rd), .en(r18we_t), .clk(clk), .Q(x18q_t));  // open: clr
  Register #(.width(32)) x22 (.D(rd), .en(r22we_t), .clk(clk), .Q(x22q_t));  // open: clr
  Register #(.width(32)) x26 (.D(rd), .en(r26we_t), .clk(clk), .Q(x26q_t));  // open: clr
  Register #(.width(32)) x30 (.D(rd), .en(r30we_t), .clk(clk), .Q(x30q_t));  // open: clr
  Register #(.width(32)) x3 (.D(rd), .en(r3we_t), .clk(clk), .Q(x3q_t));  // open: clr
  Register #(.width(32)) x7 (.D(rd), .en(r7we_t), .clk(clk), .Q(x7q_t));  // open: clr
  Register #(.width(32)) x11 (.D(rd), .en(r11we_t), .clk(clk), .Q(x11q_t));  // open: clr
  Register #(.width(32)) x15 (.D(rd), .en(r15we_t), .clk(clk), .Q(x15q_t));  // open: clr
  Register #(.width(32)) x19 (.D(rd), .en(r19we_t), .clk(clk), .Q(x19q_t));  // open: clr
  Register #(.width(32)) x23 (.D(rd), .en(r23we_t), .clk(clk), .Q(x23q_t));  // open: clr
  Register #(.width(32)) x27 (.D(rd), .en(r27we_t), .clk(clk), .Q(x27q_t));  // open: clr
  Register #(.width(32)) x31 (.D(rd), .en(r31we_t), .clk(clk), .Q(x31q_t));  // open: clr
  Multiplexer #(.select(5), .width(32)) multiplexer_1 (
    .in0({32{1'b0}}), .in1(x1q_t), .in2(x2q_t), .in3(x3q_t), .in4(x4q_t), .in5(x5q_t), .in6(x6q_t),
    .in7(x7q_t), .in8(x8q_t), .in9(x9q_t), .in10(x10q_t), .in11(x11q_t), .in12(x12q_t), .in13(x13q_t),
    .in14(x14q_t), .in15(x15q_t), .in16(x16q_t), .in17(x17q_t), .in18(x18q_t), .in19(x19q_t), .in20(x20q_t),
    .in21(x21q_t), .in22(x22q_t), .in23(x23q_t), .in24(x24q_t), .in25(x25q_t), .in26(x26q_t), .in27(x27q_t),
    .in28(x28q_t), .in29(x29q_t), .in30(x30q_t), .in31(x31q_t), .out(rs1), .sel(rsi1));
  Multiplexer #(.select(5), .width(32)) multiplexer_2 (
    .in0({32{1'b0}}), .in1(x1q_t), .in2(x2q_t), .in3(x3q_t), .in4(x4q_t), .in5(x5q_t), .in6(x6q_t),
    .in7(x7q_t), .in8(x8q_t), .in9(x9q_t), .in10(x10q_t), .in11(x11q_t), .in12(x12q_t), .in13(x13q_t),
    .in14(x14q_t), .in15(x15q_t), .in16(x16q_t), .in17(x17q_t), .in18(x18q_t), .in19(x19q_t), .in20(x20q_t),
    .in21(x21q_t), .in22(x22q_t), .in23(x23q_t), .in24(x24q_t), .in25(x25q_t), .in26(x26q_t), .in27(x27q_t),
    .in28(x28q_t), .in29(x29q_t), .in30(x30q_t), .in31(x31q_t), .out(rs2), .sel(rsi2));

  // Other names for the same wires on the sheet: clk_t = clk; rd_t[31:0] = rd; rdi_t[4:0] = rdi; rs1_t[31:0] = rs1;
  //   rs2_t[31:0] = rs2; rsi1_t[4:0] = rsi1; rsi2_t[4:0] = rsi2
endmodule

module RegCtl (
  input  [31:0] rsi1,
  input  [31:0] rsi1_2,
  input  [31:0] rsi2,
  input  [31:0] rsi2_2,
  input  isFPU,
  output [31:0] rs1,
  output [31:0] rs2
);

  Multiplexer #(.width(32)) multiplexer_1 (.in0(rsi1), .in1(rsi1_2), .out(rs1), .sel(isFPU));
  Multiplexer #(.width(32)) multiplexer_2 (.in0(rsi2), .in1(rsi2_2), .out(rs2), .sel(isFPU));
endmodule

module PHT (
  input  [9:0] in_1,
  input  WE,
  input  D,
  input  in_4,
  output out_5
);

  wire and_1_out, and_2_out, and_3_out, and_4_out, and_5_out, and_6_out, d_ff_1_q, d_ff_2_q, d_ff_2_qn,
       or_1_out, or_2_out, or_4_out, ram_1_dout, register_1_q;

  Register #(.width(1)) register_1 (.D(D), .clk(in_4), .Q(register_1_q));  // open: en, clr
  RAM #(.addrWidth(10), .dataWidth(1)) ram_1 (
    .addr(in_1), .we(WE), .clk(in_4), .din(D), .dout(ram_1_dout));  // open: oe
  or or_1 (or_1_out, ram_1_dout, register_1_q);
  and and_1 (and_1_out, d_ff_2_q, or_1_out);
  or or_2 (or_2_out, and_1_out, and_2_out, and_3_out);
  and and_2 (and_2_out, or_1_out, d_ff_1_q);
  and and_3 (and_3_out, d_ff_1_q, d_ff_2_q);
  D_Flip_Flop d_ff_1 (.D(or_2_out), .clk(in_4), .Q(d_ff_1_q));  // open: Qn, preset, reset
  and and_4 (and_4_out, or_1_out, d_ff_1_q);
  and and_5 (and_5_out, or_1_out, d_ff_2_qn);
  and and_6 (and_6_out, d_ff_1_q, d_ff_2_qn);
  buf or_3 (out_5, d_ff_1_q);  // OR_Gate
  or or_4 (or_4_out, and_4_out, and_5_out, and_6_out);
  D_Flip_Flop d_ff_2 (.D(or_4_out), .clk(in_4), .Q(d_ff_2_q), .Qn(d_ff_2_qn));  // open: preset, reset
endmodule

module valid (
  input  [31:0] in_1,
  output out_2
);

  or or_1 (out_2, in_1[15], in_1[0], in_1[1], in_1[2], in_1[3], in_1[4], in_1[5], in_1[6], in_1[7], in_1[8], in_1[9], in_1[10], in_1[11], in_1[12], in_1[13], in_1[14], in_1[16], in_1[17], in_1[18], in_1[19], in_1[20], in_1[21], in_1[22], in_1[23], in_1[24], in_1[25], in_1[26], in_1[27], in_1[28], in_1[29], in_1[30], in_1[31]);
endmodule

module LoadByte (
  input  [31:0] A,
  input  [31:0] lw,
  output [31:0] lb,
  output [31:0] lbu
);

  wire [4:0] bitselector_1_out;
  wire [7:0] bitselector_2_out;
  wire [31:0] and_1_out, shifter_1_out, shifter_2_out, subtractor_1_out;

  assign and_1_out = A & 32'h3;  // AND_Gate and_1, 32 bits wide
  Subtractor #(.width(32)) subtractor_1 (.a(32'h3), .b(and_1_out), .out(subtractor_1_out));  // open: bin, bout
  Shifter #(.width(32)) shifter_1 (.in(subtractor_1_out), .\dist (5'b00011), .out(shifter_1_out));
  BitSelector #(.group(5), .width(32)) bitselector_1 (.in(shifter_1_out), .out(bitselector_1_out), .sel(3'b000));
  Shifter #(.shift("lr"), .width(32)) shifter_2 (.in(lw), .\dist (bitselector_1_out), .out(shifter_2_out));
  assign lbu = 32'hff & shifter_2_out;  // AND_Gate and_2, 32 bits wide
  BitSelector #(.group(8), .width(32)) bitselector_2 (.in(shifter_2_out), .out(bitselector_2_out), .sel(2'b00));
  assign lb = {{24{bitselector_2_out[7]}}, bitselector_2_out};  // Bit_Extender bit_extender_1

  // Other names for the same wires on the sheet: A_t[31:0] = A; lb_t[31:0] = lb; lbu_t[31:0] = lbu; lw_t[31:0] = lw
endmodule

module LoadHalf (
  input  [31:0] A,
  input  [31:0] lw,
  output [31:0] lh,
  output [31:0] lhu
);

  wire bitselector_1_out, not_1_out;
  wire [15:0] bitselector_2_out;

  BitSelector #(.width(32)) bitselector_1 (.in(A), .out(bitselector_1_out), .sel(5'b00001));
  BitSelector #(.group(16), .width(32)) bitselector_2 (.in(lw), .out(bitselector_2_out), .sel(not_1_out));
  not not_1 (not_1_out, bitselector_1_out);
  assign lh = {{16{bitselector_2_out[15]}}, bitselector_2_out};  // Bit_Extender bit_extender_1
  // Probe on bitselector_2_out
  assign lhu = {{16{1'b0}}, bitselector_2_out};  // Bit_Extender bit_extender_2

  // Other names for the same wires on the sheet: A_t[31:0] = A; lh_t[31:0] = lh; lhu_t[31:0] = lhu; lw_t[31:0] = lw
endmodule

module LoadCtl (
  input  [31:0] A,
  input  [31:0] lw_t,
  input  [2:0] Isel,
  input  wbsel,
  output [31:0] D
);

  wire [31:0] lb_t, lbu_t, lh_t, lhu_t, multiplexer_1_out;

  LoadByte loadbyte_1 (.A(A), .lw(lw_t), .lbu(lbu_t), .lb(lb_t));
  LoadHalf loadhalf_1 (.A(A), .lw(lw_t), .lh(lh_t), .lhu(lhu_t));
  Multiplexer #(.select(3), .width(32)) multiplexer_1 (
    .in0(lb_t), .in1(lh_t), .in2(lw_t), .in4(lbu_t), .in5(lhu_t), .out(multiplexer_1_out), .sel(Isel));  // open: in3, in6, in7
  Multiplexer #(.width(32)) multiplexer_2 (.in0(multiplexer_1_out), .in1(A), .out(D), .sel(wbsel));

  // Other names for the same wires on the sheet: A_t[31:0] = A; D_t[31:0] = D; Isel_t[2:0] = Isel; wbsel_t = wbsel
endmodule

module BranchPred (
  input  Taken,
  input  [31:0] PC,
  input  [31:0] ALU_a,
  input  clk,
  output [31:0] Tadd
);

  wire and_1_out, OE_t, or_1_out, pht_1_out_5, valid_1_out_2, WE_t;
  wire [9:0] bit_extender_1_out, xor_1_out;
  wire [31:0] ram_1_dout, register_1_q;

  Demultiplexer demultiplexer_1 (.out0(OE_t), .out1(WE_t), .in(1'b1), .sel(and_1_out));
  buf and_1 (and_1_out, Taken);  // AND_Gate
  assign bit_extender_1_out = {{9{Taken}}, Taken};  // Bit_Extender bit_extender_1
  RAM #(.addrWidth(10), .dataWidth(32)) ram_1 (
    .addr(PC[11:2]), .clk(clk), .din(ALU_a), .dout(ram_1_dout));  // open: we, oe
  assign xor_1_out = bit_extender_1_out ^ PC[11:2];  // XOR_Gate xor_1, 10 bits wide
  PHT pht_1 (.D(Taken), .in_1(xor_1_out), .WE(WE_t), .in_4(clk), .out_5(pht_1_out_5));
  Register #(.width(32)) register_1 (.D(ram_1_dout), .clk(clk), .Q(register_1_q));  // open: en, clr
  or or_1 (or_1_out, pht_1_out_5, Taken);
  Multiplexer #(.width(32)) multiplexer_1 (.in0(PC), .in1(register_1_q), .out(Tadd), .sel(or_1_out));
  valid valid_1 (.in_1(register_1_q), .out_2(valid_1_out_2));

  // Other names for the same wires on the sheet: clk_t = clk
endmodule

module SCPred (
  input  D,
  input  in_2,
  output out_3
);

  wire and_1_out, and_2_out, and_3_out, and_4_out, and_5_out, and_6_out, d_ff_1_q, d_ff_2_q, d_ff_2_qn,
       or_1_out, or_3_out;

  and and_1 (and_1_out, d_ff_2_q, D);
  or or_1 (or_1_out, and_1_out, and_2_out, and_3_out);
  and and_2 (and_2_out, D, d_ff_1_q);
  and and_3 (and_3_out, d_ff_1_q, d_ff_2_q);
  D_Flip_Flop d_ff_1 (.D(or_1_out), .clk(in_2), .Q(d_ff_1_q));  // open: Qn, preset, reset
  and and_4 (and_4_out, D, d_ff_1_q);
  and and_5 (and_5_out, D, d_ff_2_qn);
  and and_6 (and_6_out, d_ff_1_q, d_ff_2_qn);
  buf or_2 (out_3, d_ff_1_q);  // OR_Gate
  or or_3 (or_3_out, and_4_out, and_5_out, and_6_out);
  D_Flip_Flop d_ff_2 (.D(or_3_out), .clk(in_2), .Q(d_ff_2_q), .Qn(d_ff_2_qn));  // open: preset, reset
endmodule

// ID/EX
module PipelineReg (
  input  [31:0] In1,
  input  Stall,
  input  [31:0] In2,
  input  [31:0] In3,
  input  clk,
  input  Flush,
  output [31:0] Out1,
  output [31:0] Out2,
  output [31:0] Out3
);

  wire not_1_out, not_2_out, not_3_out;

  Register #(.width(32)) register_1 (.D(In1), .en(not_1_out), .clk(clk), .Q(Out1), .clr(Flush));
  not not_1 (not_1_out, Stall);
  Register #(.width(32)) register_2 (.D(In2), .en(not_2_out), .clk(clk), .Q(Out2), .clr(Flush));
  not not_2 (not_2_out, Stall);
  Register #(.width(32)) register_3 (.D(In3), .en(not_3_out), .clk(clk), .Q(Out3), .clr(Flush));
  not not_3 (not_3_out, Stall);
endmodule

// EX/DMEM
module EXPipe (
  input  [31:0] In1,
  input  Stall,
  input  clk,
  input  Flush,
  output [31:0] Out1
);

  wire not_1_out, not_2_out, not_3_out;
  wire [31:0] register_2_q, register_3_q, undriven, undriven_2;

  Register #(.width(32)) register_1 (.D(In1), .en(not_1_out), .clk(clk), .Q(Out1), .clr(Flush));
  not not_1 (not_1_out, Stall);
  Register #(.width(32)) register_2 (.D(undriven), .en(not_2_out), .clk(clk), .Q(register_2_q), .clr(Flush));
  not not_2 (not_2_out, Stall);
  Register #(.width(32)) register_3 (.D(undriven_2), .en(not_3_out), .clk(clk), .Q(register_3_q), .clr(Flush));
  not not_3 (not_3_out, Stall);
endmodule

// IF/ID
module IFPipe (
  input  [31:0] In1,
  input  Stall,
  input  clk,
  input  Flush,
  output [31:0] Out1
);

  wire not_1_out, not_2_out, not_3_out;
  wire [31:0] register_2_q, register_3_q, undriven, undriven_2;

  Register #(.width(32)) register_1 (.D(In1), .en(not_1_out), .clk(clk), .Q(Out1), .clr(Flush));
  not not_1 (not_1_out, Stall);
  Register #(.width(32)) register_2 (.D(undriven), .en(not_2_out), .clk(clk), .Q(register_2_q), .clr(Flush));
  not not_2 (not_2_out, Stall);
  Register #(.width(32)) register_3 (.D(undriven_2), .en(not_3_out), .clk(clk), .Q(register_3_q), .clr(Flush));
  not not_3 (not_3_out, Stall);
endmodule

module HazardCtl (
  input  BrEq,
  input  BrLt,
  input  [31:0] ins,
  input  Taken,
  output BNE,
  output Stall
);

  wire and_1_out, and_2_out, and_3_out, and_4_out, and_5_out, not_1_out, or_2_out, taken_t;
  wire [18:0] A_t;

  ROM #(.addrWidth(9), .dataWidth(19)) rom_1 (
    .addr({ins[30], ins[14:12], ins[6:2]}), .data({A_t[18:17], BNE, A_t[15:0]}));
  and and_1 (and_1_out, Taken, A_t[14]);
  and and_2 (and_2_out, Taken, A_t[18]);
  Clock clock_1 ();  // open: out
  or or_1 (Stall, and_1_out, and_2_out);
  not not_1 (not_1_out, BrLt);
  or or_2 (or_2_out, BrEq, not_1_out);
  and and_3 (and_3_out, A_t[18], BrEq);
  and and_4 (and_4_out, A_t[15], BrLt);
  and and_5 (and_5_out, or_2_out, A_t[14]);
  or or_3 (taken_t, A_t[11], and_3_out, and_4_out, and_5_out);

  // Other names for the same wires on the sheet: i2_t = ins[2]; i3_t = ins[3]; i4_t = ins[4]; i5_t = ins[5];
  //   i6_t = ins[6]; i12_t = ins[12]; i13_t = ins[13]; i14_t = ins[14]; i30_t = ins[30]; asel_t = A_t[0];
  //   bsel_t = A_t[1]; is0_t = A_t[2]; is1_t = A_t[3]; is2_t = A_t[4]; regwena_t = A_t[5]; as0_t = A_t[6];
  //   as1_t = A_t[7]; as2_t = A_t[8]; as3_t = A_t[9]; isFPU_t = A_t[10]; jal_t = A_t[11]; bgeu_t = A_t[12];
  //   bltu_t = A_t[13]; bge_t = A_t[14]; blt_t = A_t[15]; A_t[16] = BNE; bne_t = BNE; PCsel_t = A_t[17];
  //   beq_t = A_t[18]

  // Notes on the sheet:
  //   contents of rom_1 (hex, n*v repeats v):
  //   4*0 22 7*0 20 7*0 420 0 0 0 6000b 11*0 62 7*0 60 7*0 460 0 0 0 3000b 11*0 a2 7*0 a0 7*0 4a0 15*0 e2
  //   7*0 e0 23*0 122 7*0 120 11*0 2800b 11*0 162 7*0 160 11*0 2400b 11*0 1a2 7*0 1a0 11*0 2200b 11*0 1e2
  //   7*0 1e0 11*0 2100b 11*0 22 7*0 220 7*0 620 143*0 362 7*0 360 78*0 2080f
endmodule

// DMEM/WB
module DMEMpipe (
  input  [31:0] In1,
  input  Stall,
  input  [31:0] In2,
  input  [31:0] In3,
  input  clk,
  input  Flush,
  output [31:0] Out1,
  output [31:0] Out2,
  output [31:0] Out3
);

  wire not_1_out, not_2_out, not_3_out;

  Register #(.width(32)) register_1 (.D(In1), .en(not_1_out), .clk(clk), .Q(Out1), .clr(Flush));
  not not_1 (not_1_out, Stall);
  Register #(.width(32)) register_2 (.D(In2), .en(not_2_out), .clk(clk), .Q(Out2), .clr(Flush));
  not not_2 (not_2_out, Stall);
  Register #(.width(32)) register_3 (.D(In3), .en(not_3_out), .clk(clk), .Q(Out3), .clr(Flush));
  not not_3 (not_3_out, Stall);
endmodule

module Branch (
  input  in_1
);

  wire clock_1_out, d_ff_1_q, d_ff_2_q, d_ff_3_q, d_ff_4_q;

  D_Flip_Flop d_ff_1 (.D(in_1), .clk(clock_1_out), .Q(d_ff_1_q));  // open: Qn, preset, reset
  Clock clock_1 (.out(clock_1_out));
  D_Flip_Flop d_ff_2 (.D(d_ff_1_q), .clk(clock_1_out), .Q(d_ff_2_q));  // open: Qn, preset, reset
  D_Flip_Flop d_ff_3 (.D(d_ff_2_q), .clk(clock_1_out), .Q(d_ff_3_q));  // open: Qn, preset, reset
  D_Flip_Flop d_ff_4 (.D(d_ff_3_q), .clk(clock_1_out), .Q(d_ff_4_q));  // open: Qn, preset, reset
  SCPred scpred_1 ();  // open: D, in_2, out_3
endmodule
